# Fritzing sketch Wiring (saved by Fritzing 0.9.3b)
breadboards: 1

parts:
  C1 = Electrolytic Capacitor [capacitance=1µF package="100 mil [THT, electrolytic]"]
  Raspberry_Pi_1 = Raspberry Pi 4 [part_number=RPI-4-b]
  S1 = Momentary Switch [package=ksa_sealed_tac_switch]  # not connected
  S2 = Momentary Switch [package=ksa_sealed_tac_switch]  # not connected
  S3 = Momentary Switch [package=ksa_sealed_tac_switch]  # not connected
  S4 = Momentary Switch [package=ksa_sealed_tac_switch]  # not connected

nets:
  N1: C1.-, Raspberry_Pi_1.GND
  N2: C1.+, Raspberry_Pi_1.5V

custom parts:
  Raspberry Pi 4: The RPi4, a faster version of the awesome Raspberry Pi 2 B ARM Board with 40 pin gpio. Ready for special Raspberry Pi B+ and RPi2 Hat (Hardware attached (on) top)
